// Logisim project model.circ as structural Verilog: 8 circuits, main circuit main
module main (
  input  rx,
  output cts,
  output sound_out
);

  wire cmd_1_mixer_we_mix_shift, cmd_1_noise_i_mode, cmd_1_noise_we_mode, cmd_1_noise_we_period,
       cmd_1_noise_we_vol, cmd_1_processing, cmd_1_ram_we, cmd_1_sampler_i_chan_enable_we,
       cmd_1_sampler_i_chan_we_phase, cmd_1_sampler_i_chan_we_rate, cmd_1_sampler_i_chan_we_sample,
       cmd_1_sampler_i_chan_we_vol, sampler_1_busy, uart_cmd_1_o_cmd_ready;
  wire [2:0] cmd_1_mixer_i_mix_shift, cmd_1_sampler_i_chan_select;
  wire [3:0] cmd_1_noise_i_vol, cmd_1_sampler_i_chan_i_vol, sample_ram_1_rdata_0, sample_ram_1_rdata_1;
  wire [7:0] cmd_1_noise_i_period, cmd_1_ram_waddr, cmd_1_ram_wdata, cmd_1_sampler_i_chan_enable,
       cmd_1_sampler_i_chan_i_length, cmd_1_sampler_i_chan_i_start, mixer_1_o, noise_1_o, sampler_1_ram_addr,
       uart_cmd_1_o_cmd_arg_0, uart_cmd_1_o_cmd_arg_1, uart_cmd_1_o_cmd_arg_2, uart_cmd_1_o_cmd_op;
  wire [10:0] sampler_1_o;
  wire [23:0] cmd_1_sampler_i_chan_i_phase, cmd_1_sampler_i_chan_i_rate;

  uart_cmd uart_cmd_1 (
    .o_cmd_ready(uart_cmd_1_o_cmd_ready), .o_cmd_op(uart_cmd_1_o_cmd_op),
    .o_cmd_arg_0(uart_cmd_1_o_cmd_arg_0), .o_cmd_arg_1(uart_cmd_1_o_cmd_arg_1),
    .o_cmd_arg_2(uart_cmd_1_o_cmd_arg_2), .processing(cmd_1_processing), .rx(rx), .cts(cts));
  cmd cmd_1 (
    .i_cmd_ready(uart_cmd_1_o_cmd_ready), .i_cmd_op(uart_cmd_1_o_cmd_op),
    .i_cmd_arg_0(uart_cmd_1_o_cmd_arg_0), .i_cmd_arg_1(uart_cmd_1_o_cmd_arg_1),
    .i_cmd_arg_2(uart_cmd_1_o_cmd_arg_2), .busy(sampler_1_busy),
    .sampler_i_chan_enable(cmd_1_sampler_i_chan_enable),
    .sampler_i_chan_enable_we(cmd_1_sampler_i_chan_enable_we),
    .sampler_i_chan_select(cmd_1_sampler_i_chan_select),
    .sampler_i_chan_i_phase(cmd_1_sampler_i_chan_i_phase),
    .sampler_i_chan_i_rate(cmd_1_sampler_i_chan_i_rate),
    .sampler_i_chan_i_start(cmd_1_sampler_i_chan_i_start),
    .sampler_i_chan_i_length(cmd_1_sampler_i_chan_i_length),
    .sampler_i_chan_i_vol(cmd_1_sampler_i_chan_i_vol),
    .sampler_i_chan_we_phase(cmd_1_sampler_i_chan_we_phase),
    .sampler_i_chan_we_rate(cmd_1_sampler_i_chan_we_rate),
    .sampler_i_chan_we_sample(cmd_1_sampler_i_chan_we_sample),
    .sampler_i_chan_we_vol(cmd_1_sampler_i_chan_we_vol), .processing(cmd_1_processing),
    .noise_i_period(cmd_1_noise_i_period), .noise_i_mode(cmd_1_noise_i_mode),
    .noise_i_vol(cmd_1_noise_i_vol), .noise_we_period(cmd_1_noise_we_period),
    .noise_we_mode(cmd_1_noise_we_mode), .noise_we_vol(cmd_1_noise_we_vol),
    .mixer_i_mix_shift(cmd_1_mixer_i_mix_shift), .mixer_we_mix_shift(cmd_1_mixer_we_mix_shift),
    .ram_waddr(cmd_1_ram_waddr), .ram_wdata(cmd_1_ram_wdata), .ram_we(cmd_1_ram_we));  // open: sampler_i_ram_data_0, sampler_i_ram_data_1
  sampler sampler_1 (
    .i_chan_enable(cmd_1_sampler_i_chan_enable), .i_chan_enable_we(cmd_1_sampler_i_chan_enable_we),
    .i_chan_select(cmd_1_sampler_i_chan_select), .i_chan_i_phase(cmd_1_sampler_i_chan_i_phase),
    .i_chan_i_rate(cmd_1_sampler_i_chan_i_rate), .i_chan_i_start(cmd_1_sampler_i_chan_i_start),
    .i_chan_i_length(cmd_1_sampler_i_chan_i_length), .i_chan_i_vol(cmd_1_sampler_i_chan_i_vol),
    .i_chan_we_phase(cmd_1_sampler_i_chan_we_phase), .i_chan_we_rate(cmd_1_sampler_i_chan_we_rate),
    .i_chan_we_sample(cmd_1_sampler_i_chan_we_sample), .i_chan_we_vol(cmd_1_sampler_i_chan_we_vol),
    .i_ram_data_0(sample_ram_1_rdata_0), .i_ram_data_1(sample_ram_1_rdata_1), .o(sampler_1_o),
    .ram_addr(sampler_1_ram_addr), .busy(sampler_1_busy));
  sample_ram sample_ram_1 (
    .waddr(cmd_1_ram_waddr), .wdata(cmd_1_ram_wdata), .we(cmd_1_ram_we), .raddr(sampler_1_ram_addr),
    .rdata_0(sample_ram_1_rdata_0), .rdata_1(sample_ram_1_rdata_1));
  noise noise_1 (
    .i_period(cmd_1_noise_i_period), .i_mode(cmd_1_noise_i_mode), .i_vol(cmd_1_noise_i_vol),
    .we_period(cmd_1_noise_we_period), .we_mode(cmd_1_noise_we_mode), .we_vol(cmd_1_noise_we_vol),
    .o(noise_1_o));
  mixer mixer_1 (
    .sampler(sampler_1_o), .noise(noise_1_o), .i_mix_shift(cmd_1_mixer_i_mix_shift),
    .we_mix_shift(cmd_1_mixer_we_mix_shift), .o(mixer_1_o));
  pwm pwm_1 (.i(mixer_1_o), .o(sound_out));

  // Notes on the sheet:
  //   (Host)
endmodule

module cmd (
  input  i_cmd_ready,
  input  [7:0] i_cmd_op,
  input  [7:0] i_cmd_arg_0,
  input  [7:0] i_cmd_arg_1,
  input  [7:0] i_cmd_arg_2,
  input  busy,
  output [7:0] sampler_i_chan_enable,
  output sampler_i_chan_enable_we,
  output [2:0] sampler_i_chan_select,
  output [23:0] sampler_i_chan_i_phase,
  output [23:0] sampler_i_chan_i_rate,
  output [7:0] sampler_i_chan_i_start,
  output [7:0] sampler_i_chan_i_length,
  output [3:0] sampler_i_chan_i_vol,
  output sampler_i_chan_we_phase,
  output sampler_i_chan_we_rate,
  output sampler_i_chan_we_sample,
  output sampler_i_chan_we_vol,
  output [3:0] sampler_i_ram_data_0,
  output [3:0] sampler_i_ram_data_1,
  output [7:0] noise_i_period,
  output noise_i_mode,
  output [3:0] noise_i_vol,
  output noise_we_period,
  output noise_we_mode,
  output noise_we_vol,
  output [2:0] mixer_i_mix_shift,
  output mixer_we_mix_shift,
  output [7:0] ram_waddr,
  output [7:0] ram_wdata,
  output ram_we,
  output processing
);


  assign mixer_i_mix_shift = 3'b000;
  assign mixer_we_mix_shift = 1'b0;
  assign noise_i_mode = 1'b0;
  assign noise_i_period = {8{1'b0}};
  assign noise_i_vol = 4'b0000;
  assign noise_we_mode = 1'b0;
  assign noise_we_period = 1'b0;
  assign noise_we_vol = 1'b0;
  assign processing = 1'b0;
  assign ram_waddr = {8{1'b0}};
  assign ram_wdata = {8{1'b0}};
  assign ram_we = 1'b0;
  assign sampler_i_chan_enable = {8{1'b0}};
  assign sampler_i_chan_enable_we = 1'b0;
  assign sampler_i_chan_i_length = {8{1'b0}};
  assign sampler_i_chan_i_phase = {24{1'b0}};
  assign sampler_i_chan_i_rate = {24{1'b0}};
  assign sampler_i_chan_i_start = {8{1'b0}};
  assign sampler_i_chan_i_vol = 4'b0000;
  assign sampler_i_chan_select = 3'b000;
  assign sampler_i_chan_we_phase = 1'b0;
  assign sampler_i_chan_we_rate = 1'b0;
  assign sampler_i_chan_we_sample = 1'b0;
  assign sampler_i_chan_we_vol = 1'b0;
  assign sampler_i_ram_data_0 = 4'b0000;
  assign sampler_i_ram_data_1 = 4'b0000;
endmodule

module mixer (
  input  [10:0] sampler,
  input  [7:0] noise,
  input  [2:0] i_mix_shift,
  input  we_mix_shift,
  output [7:0] o
);


  assign o = {8{1'b0}};
endmodule

module noise (
  input  [7:0] i_period,
  input  i_mode,
  input  [3:0] i_vol,
  input  we_period,
  input  we_mode,
  input  we_vol,
  output [7:0] o
);


  assign o = {8{1'b0}};
endmodule

module pwm (
  input  [7:0] i,
  output o
);


  assign o = 1'b0;
endmodule

module sampler (
  input  [7:0] i_chan_enable,
  input  i_chan_enable_we,
  input  [2:0] i_chan_select,
  input  [23:0] i_chan_i_phase,
  input  [23:0] i_chan_i_rate,
  input  [7:0] i_chan_i_start,
  input  [7:0] i_chan_i_length,
  input  [3:0] i_chan_i_vol,
  input  i_chan_we_phase,
  input  i_chan_we_rate,
  input  i_chan_we_sample,
  input  i_chan_we_vol,
  input  [3:0] i_ram_data_0,
  input  [3:0] i_ram_data_1,
  output [10:0] o,
  output [7:0] ram_addr,
  output busy
);


  assign busy = 1'b0;
  assign o = {11{1'b0}};
  assign ram_addr = {8{1'b0}};
endmodule

// smp ram
module sample_ram (
  input  [7:0] waddr,
  input  [7:0] wdata,
  input  we,
  input  [7:0] raddr,
  output [3:0] rdata_0,
  output [3:0] rdata_1
);


  assign rdata_0 = 4'b0000;
  assign rdata_1 = 4'b0000;
endmodule

// UART
module uart_cmd (
  input  rx,
  input  processing,
  output o_cmd_ready,
  output [7:0] o_cmd_op,
  output [7:0] o_cmd_arg_0,
  output [7:0] o_cmd_arg_1,
  output [7:0] o_cmd_arg_2,
  output cts
);


  assign cts = 1'b0;
  assign o_cmd_arg_0 = {8{1'b0}};
  assign o_cmd_arg_1 = {8{1'b0}};
  assign o_cmd_arg_2 = {8{1'b0}};
  assign o_cmd_op = {8{1'b0}};
  assign o_cmd_ready = 1'b0;
endmodule
